// Logisim project RISCV.circ as structural Verilog: 15 circuits, main circuit RISCV
module RISCV (
);

  wire clock_1_out, comparator_black_box_1_p4, iscomp_1_isw, iscomp_1_outp, isVal, lssel_1_l, lssel_1_s,
       lssel_1_usem, opdecode3_1_isl, ramprc_1_p4, ramprc_1_p5, registerfile_1_p7, undriven, wedec_1_u,
       wedec_1_we;
  wire [1:0] opdecode3_1_out_2, ramprc_1_p3;
  wire [2:0] rdecode_1_funct3;
  wire [3:0] aluop2_1_aop;
  wire [4:0] lsb5_1_shiftamnt, rdecode_1_rd, rdecode_1_rs1, rdecode_1_rs2;
  wire [6:0] rdecode_1_funct7, rdecode_1_op;
  wire [31:0] add4_1_out_2, alu_1_p5, bit_extender_1_out, gt8bts_1_cout, lbdec_1_cout, multiplexer_1_out,
       multiplexer_2_out, multiplexer_3_out, multiplexer_4_out, ram_1_p7, register_1_q, registerfile_1_p8,
       risc_vprogramrom_1_p2, UImm, WriteData;

  Clock clock_1 (.out(clock_1_out));
  Register #(.width(32)) register_1 (
    .D(add4_1_out_2), .clk(clock_1_out), .Q(register_1_q), .clr(undriven));  // open: en
  add4 add4_1 (.ln(register_1_q), .out_2(add4_1_out_2));
  wedec wedec_1 (.isVal(isVal), .OpD(opdecode3_1_out_2), .U(wedec_1_u), .WE(wedec_1_we));
  Multiplexer #(.width(32), .enable("false")) multiplexer_1 (
    .in0(WriteData), .in1(UImm), .out(multiplexer_1_out), .sel(wedec_1_u));
  RDecode rdecode_1 (
    .ln(risc_vprogramrom_1_p2), .op(rdecode_1_op), .rd(rdecode_1_rd), .funct3(rdecode_1_funct3),
    .rs1(rdecode_1_rs1), .rs2(rdecode_1_rs2), .funct7(rdecode_1_funct7));
  OpDecode3 opdecode3_1 (.in_1(risc_vprogramrom_1_p2), .out_2(opdecode3_1_out_2), .isL(opdecode3_1_isl));
  // RISC_VProgramROM risc_vprogramrom_1: pin names not known; wires that end beside it: register_1_q, risc_vprogramrom_1_p2
  // RegisterFile registerfile_1: pin names not known; wires that end beside it: multiplexer_1_out, clock_1_out, wedec_1_we, rdecode_1_rd, rdecode_1_rs1, rdecode_1_rs2, registerfile_1_p7, registerfile_1_p8
  ImmGen immgen_1 (.OpCode(opdecode3_1_out_2), .Inp(risc_vprogramrom_1_p2), .Cout(UImm));
  Multiplexer #(.select(2), .width(32), .enable("false")) multiplexer_2 (
    .in0(UImm), .in1(UImm), .in2(UImm), .in3(registerfile_1_p8), .out(multiplexer_2_out),
    .sel(opdecode3_1_out_2));
  LSB5 lsb5_1 (.in_1(multiplexer_2_out), .ShiftAmnt(lsb5_1_shiftamnt));
  ALUOP2 aluop2_1 (.funct3(rdecode_1_funct3), .funct7(rdecode_1_funct7), .op(rdecode_1_op), .AOp(aluop2_1_aop));
  // Comparator_Black_Box comparator_black_box_1: pin names not known; wires that end beside it: registerfile_1_p7, multiplexer_2_out, rdecode_1_funct3[1], comparator_black_box_1_p4
  // ALU alu_1: pin names not known; wires that end beside it: registerfile_1_p7, multiplexer_2_out, aluop2_1_aop, lsb5_1_shiftamnt, alu_1_p5
  lbdec lbdec_1 (.Cin(registerfile_1_p8), .Cout(lbdec_1_cout));
  isComp iscomp_1 (
    .Inp(rdecode_1_funct3), .Op(opdecode3_1_out_2), .isL(opdecode3_1_isl), .isW(iscomp_1_isw),
    .Outp(iscomp_1_outp));
  assign bit_extender_1_out = {{31{1'b0}}, comparator_black_box_1_p4};  // Bit_Extender bit_extender_1
  Multiplexer #(.width(32), .enable("false")) multiplexer_3 (
    .in0(alu_1_p5), .in1(bit_extender_1_out), .out(multiplexer_3_out), .sel(iscomp_1_outp));
  Multiplexer #(.width(32), .enable("false")) multiplexer_4 (
    .in0(lbdec_1_cout), .in1(registerfile_1_p8), .out(multiplexer_4_out), .sel(iscomp_1_isw));
  // RAMPRC ramprc_1: pin names not known; wires that end beside it: iscomp_1_isw, multiplexer_3_out, ramprc_1_p3, ramprc_1_p4, ramprc_1_p5, isVal
  lssel lssel_1 (
    .isVal(isVal), .OpDecode(opdecode3_1_out_2), .isL(opdecode3_1_isl), .funct3(rdecode_1_funct3),
    .s(lssel_1_s), .l(lssel_1_l), .useM(lssel_1_usem));
  // RAM ram_1: pin names not known; wires that end beside it: ramprc_1_p5, multiplexer_4_out, lssel_1_s, ramprc_1_p4, clock_1_out, lssel_1_l, ram_1_p7
  Multiplexer #(.width(32), .enable("false")) multiplexer_5 (
    .in0(multiplexer_3_out), .in1(gt8bts_1_cout), .out(WriteData), .sel(lssel_1_usem));
  gt8bts gt8bts_1 (.dIn(ram_1_p7), .sel(ramprc_1_p3), .isW(iscomp_1_isw), .cOut(gt8bts_1_cout));

  // Notes on the sheet:
  //   contents of risc_vprogramrom_1 (hex, n*v repeats v):
  //   ## desc = byte reversal ## cycles = 100  lui t0, 0x12345 addi t0, t0, 0x678 sw t0, 0(x0)  lui t0,
  //   0x13f44 addi t0, t0, 0x64c sw t0, 4(x0)   #TODO 1 #reverse word at memaddr 0 with bitmasks, store in
  //   t0 lw x28, 0(x0)  addi x14, x0, 24 addi x16, x0, 8 addi x23, x0, 16  addi x9, x0, 255 sll x6, x9,
  //   x14 sll x7, x9, x23 sll x8, x9, x16   and x10, x28, t1 and x11, x28, t2 and x12, x28, x8 and x13,
  //   x28, x9  addi x14, x0, 24 addi x16, x0, 8  sra x15, x10, x14  sll x17, x13, x14 sra x18, x11, x16
  //   sll x19, x12, x16  add x20, x15, x18  add x21, x17, x19  add x5, x20, x21     #TODO 2 #reverse word
  //   at memaddr 4 with lb/sb, store in t1  lb x6, 4(x0) lb x7, 5(x0) lb x8, 6(x0) lb x9, 7(x0)  sb x9,
  //   8(x0) sb x8, 9(x0) sb x7, 10(x0) sb x6, 11(x0)  lw x6, 8(x0)    #TODO 3 #xor both reversed words,
  //   store in t2  xor t2, t0, t1  ##expected[6] = 0x4c46f413 ##expected[5] = 0x78563412 ##expected[7] =
  //   0x3410c001
endmodule

module add4 (
  input  [31:0] ln,
  output [31:0] out_2
);

  // Incrementer #(.width(30)) incrementer_1: pin names not known; wires that end beside it: ln[31:2]

  assign out_2[1:0] = ln[1:0];
endmodule

module RDecode (
  input  [31:0] ln,
  output [6:0] op,
  output [4:0] rd,
  output [2:0] funct3,
  output [4:0] rs1,
  output [4:0] rs2,
  output [6:0] funct7
);


  assign funct3 = ln[14:12];
  assign funct7 = ln[31:25];
  assign op = ln[6:0];
  assign rd = ln[11:7];
  assign rs1 = ln[19:15];
  assign rs2 = ln[24:20];
endmodule

module ImmGen (
  input  [1:0] OpCode,
  input  [31:0] Inp,
  output [31:0] Cout
);

  wire [11:0] bit_extender_4_out;
  wire [31:0] bit_extender_1_out, bit_extender_2_out, bit_extender_3_out;

  assign bit_extender_1_out = {{20{Inp[31]}}, {Inp[31:25], Inp[11:7]}};  // Bit_Extender bit_extender_1
  assign bit_extender_2_out = {{25{Inp[31]}}, Inp[31:25]};  // Bit_Extender bit_extender_2
  assign bit_extender_3_out = {{20{Inp[31]}}, Inp[31:20]};  // Bit_Extender bit_extender_3
  assign {bit_extender_4_out[0], bit_extender_4_out[1], bit_extender_4_out[2], bit_extender_4_out[3], bit_extender_4_out[4], bit_extender_4_out[5], bit_extender_4_out[6], bit_extender_4_out[7], bit_extender_4_out[8], bit_extender_4_out[9], bit_extender_4_out[10], bit_extender_4_out[11]} = {{11{Inp[6]}}, Inp[6]};  // Bit_Extender bit_extender_4
  Multiplexer #(.select(2), .width(32), .enable("false")) multiplexer_1 (
    .in0(bit_extender_3_out), .in1(bit_extender_1_out), .in2({Inp[31:12], bit_extender_4_out}),
    .in3(bit_extender_2_out), .out(Cout), .sel(OpCode));
endmodule

module ALUOP (
  input  [2:0] funct3,
  input  [6:0] funct7,
  input  [6:0] op,
  output [3:0] AOp
);

  wire and_1_out, and_2_out, and_3_out, and_4_out, not_1_out;

  not not_1 (not_1_out, funct3[0]);
  and and_1 (and_1_out, funct3[0], funct7[5], op[5]);
  and and_2 (and_2_out, funct3[2], funct3[1]);
  and and_3 (and_3_out, funct3[1], funct3[0]);
  and and_4 (and_4_out, funct3[2], not_1_out);
  or or_1 (AOp[2], and_1_out, funct3[2]);
  or or_2 (AOp[1], funct3[0], and_2_out);
  or or_3 (AOp[3], and_3_out, and_4_out);

  assign AOp[0] = funct3[0];
endmodule

module LSB5 (
  input  [31:0] in_1,
  output [4:0] ShiftAmnt
);


  assign ShiftAmnt = in_1[4:0];
endmodule

module isComp (
  input  [2:0] Inp,
  input  [1:0] Op,
  input  isL,
  output isW,
  output Outp
);

  wire not_1_out, xnor_1_out;

  not not_1 (not_1_out, isL);
  and and_1 (isW, ~Inp[0], Inp[1], ~Inp[2]);  // AND_Gate
  xnor xnor_1 (xnor_1_out, Op[0], Op[1]);
  and and_2 (Outp, isW, xnor_1_out, not_1_out);
endmodule

module RAMPRC (
  input  isW,
  input  [31:0] inp,
  output [1:0] selR,
  output [3:0] sel,
  output [19:0] twnty,
  output isVal
);

  wire [3:0] bit_extender_1_out, twbtdc_1_out_3;

  nor nor_1 (isVal, inp[22], inp[23], inp[24], inp[25], inp[26], inp[28], inp[29], inp[30], inp[31], inp[27]);
  twbtdc twbtdc_1 (.b0(inp[0]), .b1(inp[1]), .out_3(twbtdc_1_out_3));
  assign bit_extender_1_out = {{3{1'b1}}, isW};  // Bit_Extender bit_extender_1
  Multiplexer #(.width(4), .enable("false")) multiplexer_1 (
    .in0(twbtdc_1_out_3), .in1(bit_extender_1_out), .out(sel), .sel(isW));

  assign selR = inp[1:0];
  assign twnty = inp[21:2];
endmodule

module twbtdc (
  input  b0,
  input  b1,
  output [3:0] out_3
);

  wire not_1_out, not_2_out, not_3_out, not_4_out;

  and and_1 (out_3[3], b0, b1);
  not not_1 (not_1_out, b0);
  not not_2 (not_2_out, b1);
  not not_3 (not_3_out, b0);
  not not_4 (not_4_out, b1);
  and and_2 (out_3[2], not_1_out, b1);
  and and_3 (out_3[1], b0, not_2_out);
  and and_4 (out_3[0], not_3_out, not_4_out);
endmodule

module lssel (
  input  isVal,
  input  [1:0] OpDecode,
  input  isL,
  input  [2:0] funct3,
  output s,
  output l,
  output useM
);

  wire and_1_out, nor_1_out, nor_2_out;

  and and_1 (and_1_out, ~OpDecode[1], OpDecode[0]);  // AND_Gate
  nor nor_1 (nor_1_out, OpDecode[1], OpDecode[0]);
  nor nor_2 (nor_2_out, funct3[0], funct3[2]);
  and and_2 (s, isVal, and_1_out);
  and and_3 (l, isVal, nor_1_out, nor_2_out);
  and and_4 (useM, nor_1_out, isL, nor_2_out);
endmodule

module wedec (
  input  isVal,
  input  [1:0] OpD,
  output U,
  output WE
);

  wire and_1_out, not_1_out, not_2_out;

  and and_1 (and_1_out, OpD[0], ~OpD[1]);  // AND_Gate
  and and_2 (U, ~OpD[0], OpD[1]);  // AND_Gate
  not not_1 (not_1_out, and_1_out);
  not not_2 (not_2_out, isVal);
  or or_1 (WE, not_2_out, not_1_out);
endmodule

module OpDecode3 (
  input  [31:0] in_1,
  output [1:0] out_2,
  output isL
);

  wire not_2_out;

  not not_1 (isL, in_1[4]);
  and and_1 (out_2[1], in_1[5], in_1[4]);
  not not_2 (not_2_out, in_1[2]);
  and and_2 (out_2[0], in_1[5], not_2_out);
endmodule

module gt8bts (
  input  [31:0] dIn,
  input  [1:0] sel,
  input  isW,
  output [31:0] cOut
);

  wire [7:0] multiplexer_1_out;
  wire [31:0] bit_extender_1_out;

  Multiplexer #(.select(2), .width(8), .enable("false")) multiplexer_1 (
    .in0(dIn[7:0]), .in1(dIn[15:8]), .in2(dIn[23:16]), .in3(dIn[31:24]), .out(multiplexer_1_out), .sel(sel));
  assign bit_extender_1_out = {{24{multiplexer_1_out[7]}}, multiplexer_1_out};  // Bit_Extender bit_extender_1
  Multiplexer #(.width(32), .enable("false")) multiplexer_2 (
    .in0(bit_extender_1_out), .in1(dIn), .out(cOut), .sel(isW));
endmodule

module lbdec (
  input  [31:0] Cin,
  output [31:0] Cout
);


  assign Cout = {Cin[7:0], Cin[7:0], Cin[7:0], Cin[7:0]};
endmodule

module ALUOP2 (
  input  [2:0] funct3,
  input  [6:0] funct7,
  input  [6:0] op,
  output [3:0] AOp
);

  wire and_1_out, and_2_out, and_3_out, and_4_out, and_5_out, and_6_out, not_1_out, not_2_out, not_3_out,
       not_4_out;

  not not_1 (not_1_out, funct3[0]);
  not not_2 (not_2_out, funct3[1]);
  and and_1 (and_1_out, funct3[2], funct3[1]);
  not not_3 (not_3_out, funct3[2]);
  not not_4 (not_4_out, funct3[1]);
  and and_2 (and_2_out, funct3[1], funct3[0]);
  and and_3 (and_3_out, funct3[2], not_1_out);
  and and_4 (and_4_out, not_2_out, funct7[5], op[5]);
  and and_5 (and_5_out, funct3[0], funct7[5], op[5]);
  or or_1 (AOp[1], funct3[0], and_1_out);
  and and_6 (and_6_out, not_3_out, not_4_out, funct7[5], op[5]);
  or or_2 (AOp[3], and_2_out, and_3_out);
  or or_3 (AOp[2], and_4_out, and_5_out, funct3[2]);
  or or_4 (AOp[0], and_6_out, funct3[0]);
endmodule
